// Logisim project EachLatch.circ as structural Verilog: 1 circuit, main circuit main
module main (
  input  S__or_J,
  input  R__or_K,
  output LED
);

  wire button_1_out, not_1_out;

  Button button_1 (.out(button_1_out));
  not not_1 (not_1_out, R__or_K);
  J_K_Flip_Flop j_k_ff_1 (.J(S__or_J), .clk(button_1_out), .K(not_1_out), .Q(LED));  // open: Qn, preset, en, reset

  // Notes on the sheet:
  //   Clock
endmodule
