// Logisim project Final.circ as structural Verilog: 5 circuits, main circuit main
module main (
  input  in_1,
  input  in_2,
  input  in_3,
  input  in_4,
  input  in_5,
  input  in_6,
  input  in_7,
  input  in_8,
  input  in_9,
  input  in_10,
  input  in_11,
  input  in_12,
  input  in_13,
  input  in_14,
  input  in_15,
  input  in_16,
  output [1:0] out_17,
  output [1:0] out_18
);

  wire multiplexer_1_out, multiplexer_2_out, priority_encoder_1_p1, priority_encoder_1_p2,
       priority_encoder_1_p4, priority_encoder_1_p5, priority_encoder_2_p4, priority_encoder_2_p5,
       row_input_1_out_5, row_input_1_out_6, row_input_1_out_7, row_input_1_out_8, row_input_2_out_5,
       row_input_2_out_6, row_input_2_out_7, row_input_2_out_8, row_input_3_out_5, row_input_3_out_6,
       row_input_3_out_7, row_input_3_out_8, row_input_4_out_5, row_input_4_out_6, row_input_4_out_7,
       row_input_4_out_8;

  // Priority_Encoder #(.select(2)) priority_encoder_1: pin names not known; wires that end beside it: priority_encoder_1_p1, priority_encoder_1_p2, out_17, priority_encoder_1_p4, priority_encoder_1_p5
  Multiplexer #(.select(2), .enable("false")) multiplexer_1 (
    .in0(in_1), .in1(in_5), .in2(in_9), .in3(in_13), .out(multiplexer_1_out), .sel(out_17));
  Multiplexer #(.select(2), .enable("false")) multiplexer_2 (
    .in0(in_2), .in1(in_6), .in2(in_10), .in3(in_14), .out(multiplexer_2_out), .sel(out_17));
  // Priority_Encoder #(.select(2)) priority_encoder_2: pin names not known; wires that end beside it: multiplexer_1_out, multiplexer_2_out, out_18, priority_encoder_2_p4, priority_encoder_2_p5
  Multiplexer #(.select(2), .enable("false")) multiplexer_3 (
    .in0(in_3), .in1(in_7), .in2(in_11), .in3(in_15), .out(priority_encoder_2_p4), .sel(out_17));
  Multiplexer #(.select(2), .enable("false")) multiplexer_4 (
    .in0(in_4), .in1(in_8), .in2(in_12), .in3(in_16), .out(priority_encoder_2_p5), .sel(out_17));
  Row_Input row_input_1 (
    .in_1(in_1), .in_2(in_2), .in_3(in_3), .in_4(in_4), .out_5(row_input_1_out_5), .out_6(row_input_1_out_6),
    .out_7(row_input_1_out_7), .out_8(row_input_1_out_8), .out_9(priority_encoder_1_p1));
  Row_Input row_input_2 (
    .in_1(in_5), .in_2(in_6), .in_3(in_7), .in_4(in_8), .out_5(row_input_2_out_5), .out_6(row_input_2_out_6),
    .out_7(row_input_2_out_7), .out_8(row_input_2_out_8), .out_9(priority_encoder_1_p2));
  Row_Input row_input_3 (
    .in_1(in_9), .in_2(in_10), .in_3(in_11), .in_4(in_12), .out_5(row_input_3_out_5),
    .out_6(row_input_3_out_6), .out_7(row_input_3_out_7), .out_8(row_input_3_out_8),
    .out_9(priority_encoder_1_p4));
  Row_Input row_input_4 (
    .in_1(in_13), .in_2(in_14), .in_3(in_15), .in_4(in_16), .out_5(row_input_4_out_5),
    .out_6(row_input_4_out_6), .out_7(row_input_4_out_7), .out_8(row_input_4_out_8),
    .out_9(priority_encoder_1_p5));
  LED led_1 (.in(row_input_1_out_5));
  LED led_2 (.in(row_input_1_out_6));
  LED led_3 (.in(row_input_2_out_5));
  LED led_4 (.in(row_input_2_out_6));
  LED led_5 (.in(row_input_3_out_6));
  LED led_6 (.in(row_input_3_out_5));
  LED led_7 (.in(row_input_4_out_6));
  LED led_8 (.in(row_input_4_out_5));
  LED led_9 (.in(row_input_1_out_7));
  LED led_10 (.in(row_input_1_out_8));
  LED led_11 (.in(row_input_2_out_8));
  LED led_12 (.in(row_input_2_out_7));
  LED led_13 (.in(row_input_3_out_8));
  LED led_14 (.in(row_input_3_out_7));
  LED led_15 (.in(row_input_4_out_8));
  LED led_16 (.in(row_input_4_out_7));
endmodule

module Row_Input (
  input  in_1,
  input  in_2,
  input  in_3,
  input  in_4,
  output out_5,
  output out_6,
  output out_7,
  output out_8,
  output out_9
);

  or or_1 (out_9, in_1, in_2, in_3, in_4);

  assign out_5 = in_1;
  assign out_6 = in_2;
  assign out_7 = in_3;
  assign out_8 = in_4;
endmodule

module Input_circuit (
  input  in_1,
  input  in_2,
  input  in_3,
  input  in_4,
  input  in_5,
  input  in_6,
  input  in_7,
  input  in_8,
  input  in_9,
  input  in_10,
  input  in_11,
  input  in_12,
  input  in_13,
  input  in_14,
  input  in_15,
  input  in_16,
  output [1:0] out_17,
  output [1:0] out_18
);

  wire multiplexer_1_out, multiplexer_2_out, priority_encoder_1_p1, priority_encoder_1_p2,
       priority_encoder_1_p4, priority_encoder_1_p5, priority_encoder_2_p4, priority_encoder_2_p5,
       row_input_1_out_5, row_input_1_out_6, row_input_1_out_7, row_input_1_out_8, row_input_2_out_5,
       row_input_2_out_6, row_input_2_out_7, row_input_2_out_8, row_input_3_out_5, row_input_3_out_6,
       row_input_3_out_7, row_input_3_out_8, row_input_4_out_5, row_input_4_out_6, row_input_4_out_7,
       row_input_4_out_8;

  // Priority_Encoder #(.select(2)) priority_encoder_1: pin names not known; wires that end beside it: priority_encoder_1_p1, priority_encoder_1_p2, out_17, priority_encoder_1_p4, priority_encoder_1_p5
  Multiplexer #(.select(2), .enable("false")) multiplexer_1 (
    .in0(in_1), .in1(in_5), .in2(in_9), .in3(in_13), .out(multiplexer_1_out), .sel(out_17));
  Multiplexer #(.select(2), .enable("false")) multiplexer_2 (
    .in0(in_2), .in1(in_6), .in2(in_10), .in3(in_14), .out(multiplexer_2_out), .sel(out_17));
  // Priority_Encoder #(.select(2)) priority_encoder_2: pin names not known; wires that end beside it: multiplexer_1_out, multiplexer_2_out, out_18, priority_encoder_2_p4, priority_encoder_2_p5
  Multiplexer #(.select(2), .enable("false")) multiplexer_3 (
    .in0(in_3), .in1(in_7), .in2(in_11), .in3(in_15), .out(priority_encoder_2_p4), .sel(out_17));
  Multiplexer #(.select(2), .enable("false")) multiplexer_4 (
    .in0(in_4), .in1(in_8), .in2(in_12), .in3(in_16), .out(priority_encoder_2_p5), .sel(out_17));
  Row_Input row_input_1 (
    .in_1(in_1), .in_2(in_2), .in_3(in_3), .in_4(in_4), .out_5(row_input_1_out_5), .out_6(row_input_1_out_6),
    .out_7(row_input_1_out_7), .out_8(row_input_1_out_8), .out_9(priority_encoder_1_p1));
  Row_Input row_input_2 (
    .in_1(in_5), .in_2(in_6), .in_3(in_7), .in_4(in_8), .out_5(row_input_2_out_5), .out_6(row_input_2_out_6),
    .out_7(row_input_2_out_7), .out_8(row_input_2_out_8), .out_9(priority_encoder_1_p2));
  Row_Input row_input_3 (
    .in_1(in_9), .in_2(in_10), .in_3(in_11), .in_4(in_12), .out_5(row_input_3_out_5),
    .out_6(row_input_3_out_6), .out_7(row_input_3_out_7), .out_8(row_input_3_out_8),
    .out_9(priority_encoder_1_p4));
  Row_Input row_input_4 (
    .in_1(in_13), .in_2(in_14), .in_3(in_15), .in_4(in_16), .out_5(row_input_4_out_5),
    .out_6(row_input_4_out_6), .out_7(row_input_4_out_7), .out_8(row_input_4_out_8),
    .out_9(priority_encoder_1_p5));
  LED led_1 (.in(row_input_1_out_5));
  LED led_2 (.in(row_input_1_out_6));
  LED led_3 (.in(row_input_2_out_6));
  LED led_4 (.in(row_input_2_out_5));
  LED led_5 (.in(row_input_3_out_5));
  LED led_6 (.in(row_input_3_out_6));
  LED led_7 (.in(row_input_4_out_6));
  LED led_8 (.in(row_input_4_out_5));
  LED led_9 (.in(row_input_1_out_7));
  LED led_10 (.in(row_input_1_out_8));
  LED led_11 (.in(row_input_2_out_7));
  LED led_12 (.in(row_input_2_out_8));
  LED led_13 (.in(row_input_3_out_7));
  LED led_14 (.in(row_input_3_out_8));
  LED led_15 (.in(row_input_4_out_7));
  LED led_16 (.in(row_input_4_out_8));
endmodule

module Output_circuit (
  input  [1:0] in_1,
  input  [1:0] in_2
);

  wire decoder_1_out0, decoder_1_out1, decoder_1_out2, decoder_1_out3, decoder_2_out0, decoder_2_out1,
       decoder_2_out2, decoder_2_out3, row_output_1_out_6, row_output_1_out_7, row_output_1_out_8,
       row_output_1_out_9, row_output_2_out_6, row_output_2_out_7, row_output_2_out_8, row_output_2_out_9,
       row_output_3_out_6, row_output_3_out_7, row_output_3_out_8, row_output_3_out_9, row_output_4_out_6,
       row_output_4_out_7, row_output_4_out_8, row_output_4_out_9;

  Decoder #(.select(2), .enable("false")) decoder_1 (
    .out0(decoder_1_out0), .out1(decoder_1_out1), .out2(decoder_1_out2), .out3(decoder_1_out3), .sel(in_1));
  Decoder #(.select(2), .enable("false")) decoder_2 (
    .out0(decoder_2_out0), .out1(decoder_2_out1), .out2(decoder_2_out2), .out3(decoder_2_out3), .sel(in_2));
  Row_Output row_output_1 (
    .in_1(decoder_1_out0), .in_2(decoder_2_out0), .in_3(decoder_2_out1), .in_4(decoder_2_out2),
    .in_5(decoder_2_out3), .out_6(row_output_1_out_6), .out_7(row_output_1_out_7),
    .out_8(row_output_1_out_8), .out_9(row_output_1_out_9));
  Row_Output row_output_2 (
    .in_1(decoder_1_out1), .in_2(decoder_2_out0), .in_3(decoder_2_out1), .in_4(decoder_2_out2),
    .in_5(decoder_2_out3), .out_6(row_output_2_out_6), .out_7(row_output_2_out_7),
    .out_8(row_output_2_out_8), .out_9(row_output_2_out_9));
  Row_Output row_output_3 (
    .in_1(decoder_1_out2), .in_2(decoder_2_out0), .in_3(decoder_2_out1), .in_4(decoder_2_out2),
    .in_5(decoder_2_out3), .out_6(row_output_3_out_6), .out_7(row_output_3_out_7),
    .out_8(row_output_3_out_8), .out_9(row_output_3_out_9));
  Row_Output row_output_4 (
    .in_1(decoder_1_out3), .in_2(decoder_2_out0), .in_3(decoder_2_out1), .in_4(decoder_2_out2),
    .in_5(decoder_2_out3), .out_6(row_output_4_out_6), .out_7(row_output_4_out_7),
    .out_8(row_output_4_out_8), .out_9(row_output_4_out_9));
  LED led_1 (.in(row_output_1_out_6));
  LED led_2 (.in(row_output_2_out_6));
  LED led_3 (.in(row_output_3_out_6));
  LED led_4 (.in(row_output_4_out_6));
  LED led_5 (.in(row_output_1_out_7));
  LED led_6 (.in(row_output_2_out_7));
  LED led_7 (.in(row_output_3_out_7));
  LED led_8 (.in(row_output_4_out_7));
  LED led_9 (.in(row_output_1_out_8));
  LED led_10 (.in(row_output_2_out_8));
  LED led_11 (.in(row_output_3_out_8));
  LED led_12 (.in(row_output_4_out_8));
  LED led_13 (.in(row_output_1_out_9));
  LED led_14 (.in(row_output_2_out_9));
  LED led_15 (.in(row_output_3_out_9));
  LED led_16 (.in(row_output_4_out_9));
endmodule

module Row_Output (
  input  in_1,
  input  in_2,
  input  in_3,
  input  in_4,
  input  in_5,
  output out_6,
  output out_7,
  output out_8,
  output out_9
);

  and and_1 (out_6, in_1, in_2);
  and and_2 (out_7, in_1, in_3);
  and and_3 (out_8, in_1, in_4);
  and and_4 (out_9, in_1, in_5);
endmodule
