// Logisim project INPUT_complete.circ as structural Verilog: 4 circuits, main circuit 3-out Toggle IC
module _3_out_Toggle_IC (
  input  in_1,
  output out_2,
  output out_3
);

  wire t_ff_1_q;

  T_Flip_Flop t_ff_1 (.clk(in_1), .T(1'b1), .Q(t_ff_1_q), .Qn(out_2));  // open: preset, reset, en
  T_Flip_Flop t_ff_2 (.clk(t_ff_1_q), .T(1'b1), .Qn(out_3));  // open: Q, preset, reset, en

  // Notes on the sheet:
  //   This is my Toggle IC!
  //   Observe its operation in the next slide...
endmodule

module Main (
  output [1:0] out_1
);

  wire button_1_out, button_2_out, button_3_out, button_4_out, button_5_out, cell_selector_1_out_5,
       cell_selector_1_out_6, cell_selector_1_out_7, cell_selector_1_out_8, demultiplexer_1_out0,
       demultiplexer_1_out1, demultiplexer_1_out2, demultiplexer_1_out3, row_latches_1_out_6,
       row_latches_1_out_7, row_latches_1_out_8, row_latches_1_out_9, row_latches_2_out_6,
       row_latches_2_out_7, row_latches_2_out_8, row_latches_2_out_9, row_latches_3_out_6,
       row_latches_3_out_7, row_latches_3_out_8, row_latches_3_out_9, row_latches_4_out_6,
       row_latches_4_out_7, row_latches_4_out_8, row_latches_4_out_9;

  Button button_1 (.out(button_1_out));
  _3_out_Toggle_IC Toggler (.out_2(out_1[0]), .out_3(out_1[1]), .in_1(button_1_out));
  Demultiplexer #(.select(2)) demultiplexer_1 (
    .out0(demultiplexer_1_out0), .out1(demultiplexer_1_out1), .out2(demultiplexer_1_out2),
    .out3(demultiplexer_1_out3), .in(1'b1), .sel(out_1));  // open: en
  LED led_1 (.in(row_latches_1_out_6));
  Row_Latches row_latches_1 (
    .Row_SET(demultiplexer_1_out0), .out_6(row_latches_1_out_6), .out_7(row_latches_1_out_7),
    .out_8(row_latches_1_out_8), .out_9(row_latches_1_out_9), .in_2(cell_selector_1_out_5),
    .in_3(cell_selector_1_out_6), .in_4(cell_selector_1_out_7), .in_5(cell_selector_1_out_8));
  LED led_2 (.in(row_latches_2_out_6));
  Row_Latches row_latches_2 (
    .Row_SET(demultiplexer_1_out1), .out_6(row_latches_2_out_6), .out_7(row_latches_2_out_7),
    .out_8(row_latches_2_out_8), .out_9(row_latches_2_out_9), .in_2(cell_selector_1_out_5),
    .in_3(cell_selector_1_out_6), .in_4(cell_selector_1_out_7), .in_5(cell_selector_1_out_8));
  LED led_3 (.in(row_latches_3_out_6));
  Row_Latches row_latches_3 (
    .Row_SET(demultiplexer_1_out2), .out_6(row_latches_3_out_6), .out_7(row_latches_3_out_7),
    .out_8(row_latches_3_out_8), .out_9(row_latches_3_out_9), .in_2(cell_selector_1_out_5),
    .in_3(cell_selector_1_out_6), .in_4(cell_selector_1_out_7), .in_5(cell_selector_1_out_8));
  LED led_4 (.in(row_latches_4_out_6));
  Row_Latches row_latches_4 (
    .Row_SET(demultiplexer_1_out3), .out_6(row_latches_4_out_6), .out_7(row_latches_4_out_7),
    .out_8(row_latches_4_out_8), .out_9(row_latches_4_out_9), .in_2(cell_selector_1_out_5),
    .in_3(cell_selector_1_out_6), .in_4(cell_selector_1_out_7), .in_5(cell_selector_1_out_8));
  Cell_Selector cell_selector_1 (
    .out_5(cell_selector_1_out_5), .out_6(cell_selector_1_out_6), .out_7(cell_selector_1_out_7),
    .out_8(cell_selector_1_out_8), .in_1(button_2_out), .in_2(button_3_out), .in_3(button_5_out),
    .in_4(button_4_out));
  Button button_2 (.out(button_2_out));
  LED led_5 (.in(row_latches_1_out_7));
  LED led_6 (.in(row_latches_1_out_8));
  LED led_7 (.in(row_latches_2_out_7));
  LED led_8 (.in(row_latches_3_out_7));
  LED led_9 (.in(row_latches_4_out_7));
  Button button_3 (.out(button_3_out));
  LED led_10 (.in(row_latches_1_out_9));
  LED led_11 (.in(row_latches_2_out_8));
  LED led_12 (.in(row_latches_2_out_9));
  LED led_13 (.in(row_latches_3_out_9));
  LED led_14 (.in(row_latches_3_out_8));
  LED led_15 (.in(row_latches_4_out_8));
  LED led_16 (.in(row_latches_4_out_9));
  Button button_4 (.out(button_4_out));
  Button button_5 (.out(button_5_out));

  // Notes on the sheet:
  //   This is my Row Toggle Button
  //   Now, observe another new change I have made.
  //   Had fun? Lets delve deeper!....
  //   This is my row selector. It uses the above DEMUX
  //   THANKS FOR WATCHING!
  //   Cell Selector
  //   This is my CELL selector. you need to observe this closely!
endmodule

module Cell_Selector (
  input  in_1,
  input  in_2,
  input  in_3,
  input  in_4,
  output out_5,
  output out_6,
  output out_7,
  output out_8
);


  assign out_5 = in_1;
  assign out_6 = in_2;
  assign out_7 = in_3;
  assign out_8 = in_4;
endmodule

module Row_Latches (
  input  Row_SET,
  input  in_2,
  input  in_3,
  input  in_4,
  input  in_5,
  output out_6,
  output out_7,
  output out_8,
  output out_9
);

  wire not_1_out, not_2_out, not_3_out, not_4_out;

  J_K_Flip_Flop j_k_ff_1 (.J(Row_SET), .clk(in_2), .K(not_1_out), .Q(out_6));  // open: Qn, preset, en, reset
  not not_1 (not_1_out, in_2);
  J_K_Flip_Flop j_k_ff_2 (.J(Row_SET), .clk(in_3), .K(not_2_out), .Q(out_7));  // open: Qn, preset, en, reset
  not not_2 (not_2_out, in_3);
  J_K_Flip_Flop j_k_ff_3 (.J(Row_SET), .clk(in_4), .K(not_3_out), .Q(out_8));  // open: Qn, preset, en, reset
  not not_3 (not_3_out, in_4);
  not not_4 (not_4_out, in_5);
  J_K_Flip_Flop j_k_ff_4 (.J(Row_SET), .clk(in_5), .K(not_4_out), .Q(out_9));  // open: Qn, preset, en, reset

  // Notes on the sheet:
  //   Note That. 
  //   THe Clock input to each JK latch is inverse of my input to the Reset.
  //   This is my set pin
  //   This is the internal circuit of each Row Latch. consisiting of 4 latches.
  //   So, once more...
  //   These are my outputs. In other words, the LEDS
  //   RESETS
  //   That's all. Anything not understood .. call me :)
  //   Excuse me! ignore this. Its a bit complicated! Just observe the corcuit design.
  //   These are my R pins
endmodule
