// Logisim project INPUT_modf.circ as structural Verilog: 3 circuits, main circuit main
module main (
  input  in_1,
  input  [1:0] Row_Binary,
  input  [1:0] Col_Binary,
  output [1:0] out_4
);

  wire button_1_out, button_2_out, button_3_out, button_4_out, button_5_out, demultiplexer_1_out0,
       demultiplexer_1_out1, demultiplexer_1_out2, demultiplexer_1_out3, demultiplexer_2_out0,
       demultiplexer_2_out1, demultiplexer_2_out2, demultiplexer_2_out3, demultiplexer_3_out0,
       demultiplexer_3_out1, demultiplexer_3_out2, demultiplexer_3_out3, row_latches_1_out_6,
       row_latches_1_out_7, row_latches_1_out_8, row_latches_1_out_9, row_latches_2_out_6,
       row_latches_2_out_7, row_latches_2_out_8, row_latches_2_out_9, row_latches_3_out_6,
       row_latches_3_out_7, row_latches_3_out_8, row_latches_3_out_9, row_latches_4_out_6,
       row_latches_4_out_7, row_latches_4_out_8, row_latches_4_out_9, undriven;

  Button button_1 (.out(button_1_out));
  Toggle_2 toggle_2_1 (.in_1(button_1_out), .out_2(out_4[0]), .out_3(out_4[1]));
  Demultiplexer #(.select(2)) demultiplexer_1 (
    .out0(demultiplexer_1_out0), .out1(demultiplexer_1_out1), .out2(demultiplexer_1_out2),
    .out3(demultiplexer_1_out3), .in(1'b1), .sel(Row_Binary));  // open: en
  Demultiplexer #(.select(2)) demultiplexer_2 (
    .out0(demultiplexer_2_out0), .out1(demultiplexer_2_out1), .out2(demultiplexer_2_out2),
    .out3(demultiplexer_2_out3), .in(1'b1), .sel(out_4));  // open: en
  LED led_1 (.in(row_latches_1_out_6));
  Row_Latches row_latches_1 (
    .Row_SET(demultiplexer_1_out0), .out_6(row_latches_1_out_6), .out_7(row_latches_1_out_7),
    .out_8(row_latches_1_out_8), .out_9(row_latches_1_out_9), .in_2(demultiplexer_3_out0),
    .in_3(demultiplexer_3_out1), .in_4(demultiplexer_3_out2), .in_5(demultiplexer_3_out3));
  LED led_2 (.in(row_latches_2_out_6));
  Row_Latches row_latches_2 (
    .Row_SET(demultiplexer_1_out1), .out_6(row_latches_2_out_6), .out_7(row_latches_2_out_7),
    .out_8(row_latches_2_out_8), .out_9(row_latches_2_out_9), .in_2(demultiplexer_3_out0),
    .in_3(demultiplexer_3_out1), .in_4(demultiplexer_3_out2), .in_5(demultiplexer_3_out3));
  LED led_3 (.in(row_latches_3_out_6));
  Row_Latches row_latches_3 (
    .Row_SET(demultiplexer_1_out2), .out_6(row_latches_3_out_6), .out_7(row_latches_3_out_7),
    .out_8(row_latches_3_out_8), .out_9(row_latches_3_out_9), .in_2(demultiplexer_3_out0),
    .in_3(demultiplexer_3_out1), .in_4(demultiplexer_3_out2), .in_5(demultiplexer_3_out3));
  LED led_4 (.in(row_latches_4_out_6));
  Row_Latches row_latches_4 (
    .Row_SET(demultiplexer_1_out3), .out_6(row_latches_4_out_6), .out_7(row_latches_4_out_7),
    .out_8(row_latches_4_out_8), .out_9(row_latches_4_out_9), .in_2(demultiplexer_3_out0),
    .in_3(demultiplexer_3_out1), .in_4(demultiplexer_3_out2), .in_5(demultiplexer_3_out3));
  Button button_2 (.out(button_2_out));
  Demultiplexer #(.select(2)) demultiplexer_3 (
    .out0(demultiplexer_3_out0), .out1(demultiplexer_3_out1), .out2(demultiplexer_3_out2),
    .out3(demultiplexer_3_out3), .in(in_1), .sel(Col_Binary), .en(undriven));
  LED led_5 (.in(row_latches_1_out_7));
  LED led_6 (.in(row_latches_2_out_7));
  LED led_7 (.in(row_latches_3_out_7));
  LED led_8 (.in(row_latches_4_out_7));
  Button button_3 (.out(button_3_out));
  LED led_9 (.in(row_latches_1_out_8));
  LED led_10 (.in(row_latches_2_out_8));
  LED led_11 (.in(row_latches_3_out_8));
  LED led_12 (.in(row_latches_4_out_8));
  Button button_4 (.out(button_4_out));
  LED led_13 (.in(row_latches_1_out_9));
  LED led_14 (.in(row_latches_2_out_9));
  LED led_15 (.in(row_latches_3_out_9));
  LED led_16 (.in(row_latches_4_out_9));
  Button button_5 (.out(button_5_out));

  // Notes on the sheet:
  //   Lets Begin the OUTPUT process
  //   Lets Begin!
  //   SO, that was my input.
  //   P1
  //   First, a few reconnections
  //   INPUT DEMUX
  //   OUTPUT Row DMX
  //   OUTPUT Column DMX
  //   Disconnect this portion during INPUT
  //   Disconnect these lines before Moving to OUTPUT
endmodule

module Row_Latches (
  input  Row_SET,
  input  in_2,
  input  in_3,
  input  in_4,
  input  in_5,
  output out_6,
  output out_7,
  output out_8,
  output out_9
);

  wire and_1_out, and_2_out, and_3_out, and_4_out;

  and and_1 (and_1_out, Row_SET, in_2);
  J_K_Flip_Flop #(.trigger("falling")) j_k_ff_1 (
    .J(Row_SET), .clk(in_2), .K(and_1_out), .Q(out_6));  // open: Qn, preset, en, reset
  and and_2 (and_2_out, Row_SET, in_3);
  J_K_Flip_Flop #(.trigger("falling")) j_k_ff_2 (
    .J(Row_SET), .clk(in_3), .K(and_2_out), .Q(out_7));  // open: Qn, preset, en, reset
  and and_3 (and_3_out, Row_SET, in_4);
  J_K_Flip_Flop #(.trigger("falling")) j_k_ff_3 (
    .J(Row_SET), .clk(in_4), .K(and_3_out), .Q(out_8));  // open: Qn, preset, en, reset
  and and_4 (and_4_out, Row_SET, in_5);
  J_K_Flip_Flop #(.trigger("falling")) j_k_ff_4 (
    .J(Row_SET), .clk(in_5), .K(and_4_out), .Q(out_9));  // open: Qn, preset, en, reset

  // Notes on the sheet:
  //   Row SET
  //   This is my set pin
  //   This is my set pin
  //   RESETS
  //   These are my R pins
  //   These are my R pins
endmodule

module Toggle_2 (
  input  in_1,
  output out_2,
  output out_3
);

  wire t_ff_1_q, t_ff_2_q;

  T_Flip_Flop #(.trigger("falling")) t_ff_1 (
    .clk(in_1), .T(1'b1), .Q(t_ff_1_q), .Qn(out_2));  // open: preset, reset, en
  T_Flip_Flop #(.trigger("falling")) t_ff_2 (
    .clk(t_ff_1_q), .T(1'b1), .Q(t_ff_2_q), .Qn(out_3));  // open: preset, reset, en

  // Notes on the sheet:
  //   This is my Toggle IC!
  //   Observe its operation in the next slide...
endmodule
