// Logisim project INPUT_subciced.circ as structural Verilog
module _3_out_Toggle_IC (
  input  in_1,
  output out_2,
  output out_3
);

  wire t_ff_1_q, t_ff_2_q;

  T_Flip_Flop t_ff_1 (.clk(in_1), .T(1'b1), .Q(t_ff_1_q), .Qn(out_2));  // open: preset, reset, en
  T_Flip_Flop t_ff_2 (.clk(t_ff_1_q), .T(1'b1), .Q(t_ff_2_q), .Qn(out_3));  // open: preset, reset, en

  // Notes on the sheet:
  //   This is my Toggle IC!
  //   Observe its operation in the next slide...
endmodule

module Main (
  output [1:0] out_1,
  output [1:0] out_2,
  output P2__P3____P4
);

  wire button_1_out, cell_selector_1_out_5, cell_selector_1_out_6, cell_selector_1_out_7,
       cell_selector_1_out_8, demultiplexer_1_out0, demultiplexer_1_out1, demultiplexer_1_out2,
       demultiplexer_1_out3, priority_encoder_1_p4, priority_encoder_1_p5, priority_encoder_1_p6,
       priority_encoder_1_p7, priority_encoder_1_p8, row_latches_1_out_6, row_latches_1_out_7,
       row_latches_1_out_8, row_latches_1_out_9, row_latches_2_out_6, row_latches_2_out_7,
       row_latches_2_out_8, row_latches_2_out_9, row_latches_3_out_6, row_latches_3_out_7,
       row_latches_3_out_8, row_latches_3_out_9, row_latches_4_out_6, row_latches_4_out_7,
       row_latches_4_out_8, row_latches_4_out_9;

  Button button_1 (.out(button_1_out));
  _3_out_Toggle_IC Toggler (.out_2(out_1[0]), .out_3(out_1[1]), .in_1(button_1_out));
  Demultiplexer #(.select(2)) demultiplexer_1 (
    .out0(demultiplexer_1_out0), .out1(demultiplexer_1_out1), .out2(demultiplexer_1_out2),
    .out3(demultiplexer_1_out3), .in(1'b1), .sel(out_1));  // open: en
  // Priority_Encoder #(.select(2)) priority_encoder_1: pin names not known; wires that end beside it: button_1_out, out_2, out_2, priority_encoder_1_p4, priority_encoder_1_p5, priority_encoder_1_p6, priority_encoder_1_p7, priority_encoder_1_p8, priority_encoder_1_p8
  or or_1 (P2__P3____P4, priority_encoder_1_p4, priority_encoder_1_p5, priority_encoder_1_p6, priority_encoder_1_p7);
  LED led_1 (.in(row_latches_1_out_6));
  Row_Latches row_latches_1 (
    .Row_SET(demultiplexer_1_out0), .out_6(row_latches_1_out_6), .out_7(row_latches_1_out_7),
    .out_8(row_latches_1_out_8), .out_9(row_latches_1_out_9), .in_2(cell_selector_1_out_5),
    .in_3(cell_selector_1_out_6), .in_4(cell_selector_1_out_7), .in_5(cell_selector_1_out_8));
  LED led_2 (.in(row_latches_2_out_6));
  Row_Latches row_latches_2 (
    .Row_SET(demultiplexer_1_out1), .out_6(row_latches_2_out_6), .out_7(row_latches_2_out_7),
    .out_8(row_latches_2_out_8), .out_9(row_latches_2_out_9), .in_2(cell_selector_1_out_5),
    .in_3(cell_selector_1_out_6), .in_4(cell_selector_1_out_7), .in_5(cell_selector_1_out_8));
  LED led_3 (.in(row_latches_3_out_6));
  Row_Latches row_latches_3 (
    .Row_SET(demultiplexer_1_out2), .out_6(row_latches_3_out_6), .out_7(row_latches_3_out_7),
    .out_8(row_latches_3_out_8), .out_9(row_latches_3_out_9), .in_2(cell_selector_1_out_5),
    .in_3(cell_selector_1_out_6), .in_4(cell_selector_1_out_7), .in_5(cell_selector_1_out_8));
  LED led_4 (.in(row_latches_4_out_6));
  Row_Latches row_latches_4 (
    .Row_SET(demultiplexer_1_out3), .out_6(row_latches_4_out_6), .out_7(row_latches_4_out_7),
    .out_8(row_latches_4_out_8), .out_9(row_latches_4_out_9), .in_2(cell_selector_1_out_5),
    .in_3(cell_selector_1_out_6), .in_4(cell_selector_1_out_7), .in_5(cell_selector_1_out_8));
  Cell_Selector cell_selector_1 (
    .out_5(cell_selector_1_out_5), .out_6(cell_selector_1_out_6), .out_7(cell_selector_1_out_7),
    .out_8(cell_selector_1_out_8), .in_1(priority_encoder_1_p4), .in_2(priority_encoder_1_p5),
    .in_3(priority_encoder_1_p6), .in_4(priority_encoder_1_p7));
  Button button_2 (.out(priority_encoder_1_p4));
  LED led_5 (.in(row_latches_1_out_7));
  LED led_6 (.in(row_latches_2_out_7));
  LED led_7 (.in(row_latches_3_out_7));
  LED led_8 (.in(row_latches_4_out_7));
  Button button_3 (.out(priority_encoder_1_p5));
  LED led_9 (.in(row_latches_1_out_9));
  LED led_10 (.in(row_latches_1_out_8));
  LED led_11 (.in(row_latches_2_out_8));
  LED led_12 (.in(row_latches_2_out_9));
  LED led_13 (.in(row_latches_3_out_8));
  LED led_14 (.in(row_latches_3_out_9));
  LED led_15 (.in(row_latches_4_out_8));
  LED led_16 (.in(row_latches_4_out_9));
  Button button_4 (.out(priority_encoder_1_p6));
  Button button_5 (.out(priority_encoder_1_p7));

  // Notes on the sheet:
  //   This is my Row Toggle Button
  //   P1
  //   Cell Selector
endmodule

module Cell_Selector (
  input  in_1,
  input  in_2,
  input  in_3,
  input  in_4,
  output out_5,
  output out_6,
  output out_7,
  output out_8
);


  assign out_5 = in_1;
  assign out_6 = in_2;
  assign out_7 = in_3;
  assign out_8 = in_4;
endmodule

module Row_Latches (
  input  Row_SET,
  input  in_2,
  input  in_3,
  input  in_4,
  input  in_5,
  output out_6,
  output out_7,
  output out_8,
  output out_9
);

  wire not_1_out, not_2_out, not_3_out, not_4_out;

  J_K_Flip_Flop j_k_ff_1 (.J(Row_SET), .clk(in_2), .K(not_1_out), .Q(out_6));  // open: Qn, preset, en, reset
  not not_1 (not_1_out, in_2);
  J_K_Flip_Flop j_k_ff_2 (.J(Row_SET), .clk(in_3), .K(not_2_out), .Q(out_7));  // open: Qn, preset, en, reset
  not not_2 (not_2_out, in_3);
  J_K_Flip_Flop j_k_ff_3 (.J(Row_SET), .clk(in_4), .K(not_3_out), .Q(out_8));  // open: Qn, preset, en, reset
  not not_3 (not_3_out, in_4);
  not not_4 (not_4_out, in_5);
  J_K_Flip_Flop j_k_ff_4 (.J(Row_SET), .clk(in_5), .K(not_4_out), .Q(out_9));  // open: Qn, preset, en, reset

  // Notes on the sheet:
  //   Note That. 
  //   THe Clock input to each JK latch is inverse of my input to the Reset.
  //   This is my set pin
  //   This is the internal circuit of each Row Latch. consisiting of 4 latches.
  //   So, once more...
  //   These are my outputs. In other words, the LEDS
  //   RESETS
  //   That's all. Anything not understood .. call me :)
  //   Excuse me! ignore this. Its a bit complicated! Just observe the corcuit design.
  //   These are my R pins
endmodule

module _4x2_Decoder (
  input  A3_MSB,
  input  A2,
  input  A1,
  input  A0_LSB,
  output Y1,
  output Y0
);

  wire and_1_out, not_1_out;

  or or_1 (Y1, A2, A3_MSB);
  not not_1 (not_1_out, A2);
  and and_1 (and_1_out, not_1_out, A1);
  or or_2 (Y0, and_1_out, A3_MSB);
endmodule

module Main2 (
  output [1:0] out_1,
  output [1:0] out_2,
  output P2__P3____P4
);

  wire and_1_out, and_2_out, and_3_out, and_4_out, and_5_out, and_6_out, and_7_out, and_8_out, and_9_out,
       and_10_out, and_11_out, and_12_out, and_13_out, and_14_out, and_15_out, and_16_out, button_1_out,
       cell_selector_1_out_5, cell_selector_1_out_6, cell_selector_1_out_7, cell_selector_1_out_8,
       collatch2_1_out_5, collatch2_1_out_6, collatch2_1_out_7, collatch2_1_out_8, demultiplexer_1_out0,
       demultiplexer_1_out1, demultiplexer_1_out2, demultiplexer_1_out3, priority_encoder_1_p4,
       priority_encoder_1_p5, priority_encoder_1_p6, priority_encoder_1_p7, rowlatch2_1_out_5,
       rowlatch2_1_out_6, rowlatch2_1_out_7, rowlatch2_1_out_8;

  Button button_1 (.out(button_1_out));
  _3_out_Toggle_IC Toggler (.out_2(out_1[0]), .out_3(out_1[1]), .in_1(button_1_out));
  Demultiplexer #(.select(2)) demultiplexer_1 (
    .out0(demultiplexer_1_out0), .out1(demultiplexer_1_out1), .out2(demultiplexer_1_out2),
    .out3(demultiplexer_1_out3), .in(1'b1), .sel(out_1));  // open: en
  // Priority_Encoder #(.select(2)) priority_encoder_1: pin names not known; wires that end beside it: button_1_out, out_2, out_2, priority_encoder_1_p4, priority_encoder_1_p5, priority_encoder_1_p6, priority_encoder_1_p7
  or or_1 (P2__P3____P4, priority_encoder_1_p4, priority_encoder_1_p5, priority_encoder_1_p6, priority_encoder_1_p7);
  ColLatch2 collatch2_1 (
    .out_5(collatch2_1_out_5), .out_6(collatch2_1_out_6), .out_7(collatch2_1_out_7),
    .out_8(collatch2_1_out_8), .in_1(demultiplexer_1_out0), .in_2(demultiplexer_1_out1),
    .in_3(demultiplexer_1_out2), .in_4(demultiplexer_1_out3));
  RowLatch2 rowlatch2_1 (
    .out_5(rowlatch2_1_out_5), .out_6(rowlatch2_1_out_6), .out_7(rowlatch2_1_out_7),
    .out_8(rowlatch2_1_out_8), .in_1(cell_selector_1_out_5), .in_3(cell_selector_1_out_7),
    .in_4(cell_selector_1_out_8), .in_2(cell_selector_1_out_6));
  and and_1 (and_1_out, collatch2_1_out_5, rowlatch2_1_out_5);
  LED led_1 (.in(and_1_out));
  and and_2 (and_2_out, collatch2_1_out_6, rowlatch2_1_out_5);
  LED led_2 (.in(and_2_out));
  LED led_3 (.in(and_3_out));
  and and_3 (and_3_out, collatch2_1_out_7, rowlatch2_1_out_5);
  LED led_4 (.in(and_4_out));
  and and_4 (and_4_out, collatch2_1_out_8, rowlatch2_1_out_5);
  Cell_Selector cell_selector_1 (
    .out_5(cell_selector_1_out_5), .out_6(cell_selector_1_out_6), .out_7(cell_selector_1_out_7),
    .out_8(cell_selector_1_out_8), .in_1(priority_encoder_1_p4), .in_2(priority_encoder_1_p5),
    .in_3(priority_encoder_1_p6), .in_4(priority_encoder_1_p7));
  Button button_2 (.out(priority_encoder_1_p4));
  and and_5 (and_5_out, collatch2_1_out_5, rowlatch2_1_out_6);
  LED led_5 (.in(and_5_out));
  and and_6 (and_6_out, collatch2_1_out_6, rowlatch2_1_out_6);
  LED led_6 (.in(and_6_out));
  and and_7 (and_7_out, collatch2_1_out_7, rowlatch2_1_out_6);
  LED led_7 (.in(and_7_out));
  LED led_8 (.in(and_8_out));
  and and_8 (and_8_out, collatch2_1_out_8, rowlatch2_1_out_6);
  Button button_3 (.out(priority_encoder_1_p5));
  LED led_9 (.in(and_9_out));
  and and_9 (and_9_out, collatch2_1_out_5, rowlatch2_1_out_7);
  LED led_10 (.in(and_10_out));
  and and_10 (and_10_out, collatch2_1_out_6, rowlatch2_1_out_7);
  LED led_11 (.in(and_11_out));
  and and_11 (and_11_out, collatch2_1_out_7, rowlatch2_1_out_7);
  and and_12 (and_12_out, collatch2_1_out_8, rowlatch2_1_out_7);
  LED led_12 (.in(and_12_out));
  Button button_4 (.out(priority_encoder_1_p6));
  Button button_5 (.out(priority_encoder_1_p7));
  LED led_13 (.in(and_13_out));
  and and_13 (and_13_out, collatch2_1_out_5, rowlatch2_1_out_8);
  LED led_14 (.in(and_14_out));
  and and_14 (and_14_out, collatch2_1_out_6, rowlatch2_1_out_8);
  and and_15 (and_15_out, collatch2_1_out_7, rowlatch2_1_out_8);
  LED led_15 (.in(and_15_out));
  and and_16 (and_16_out, collatch2_1_out_8, rowlatch2_1_out_8);
  LED led_16 (.in(and_16_out));

  // Notes on the sheet:
  //   P1
endmodule

module RowLatch2 (
  input  in_1,
  input  in_2,
  input  in_3,
  input  in_4,
  output out_5,
  output out_6,
  output out_7,
  output out_8
);

  wire not_1_out, not_2_out, not_3_out, not_4_out;

  J_K_Flip_Flop #(.trigger("falling")) j_k_ff_1 (
    .J(in_1), .clk(not_1_out), .K(in_1), .Q(out_5));  // open: Qn, preset, en, reset
  not not_1 (not_1_out, in_1);
  not not_2 (not_2_out, in_2);
  J_K_Flip_Flop #(.trigger("falling")) j_k_ff_2 (
    .J(in_2), .clk(not_2_out), .K(in_2), .Q(out_6));  // open: Qn, preset, en, reset
  J_K_Flip_Flop #(.trigger("falling")) j_k_ff_3 (
    .J(in_3), .clk(not_3_out), .K(in_3), .Q(out_7));  // open: Qn, preset, en, reset
  not not_3 (not_3_out, in_3);
  J_K_Flip_Flop #(.trigger("falling")) j_k_ff_4 (
    .J(in_4), .clk(not_4_out), .K(in_4), .Q(out_8));  // open: Qn, preset, en, reset
  not not_4 (not_4_out, in_4);

  // Notes on the sheet:
  //   Row SET
  //   This is my set pin
  //   These are my outputs. In other words, the LEDS
  //   RESETS
endmodule

module ColLatch2 (
  input  in_1,
  input  in_2,
  input  in_3,
  input  in_4,
  output out_5,
  output out_6,
  output out_7,
  output out_8
);

  wire not_1_out, not_2_out, not_3_out, not_4_out;

  J_K_Flip_Flop #(.trigger("falling")) j_k_ff_1 (
    .J(in_1), .clk(not_1_out), .K(in_1), .Q(out_5));  // open: Qn, preset, en, reset
  not not_1 (not_1_out, in_1);
  J_K_Flip_Flop #(.trigger("falling")) j_k_ff_2 (
    .J(in_2), .clk(not_2_out), .K(in_2), .Q(out_6));  // open: Qn, preset, en, reset
  not not_2 (not_2_out, in_2);
  J_K_Flip_Flop #(.trigger("falling")) j_k_ff_3 (
    .J(in_3), .clk(not_3_out), .K(in_3), .Q(out_7));  // open: Qn, preset, en, reset
  not not_3 (not_3_out, in_3);
  not not_4 (not_4_out, in_4);
  J_K_Flip_Flop #(.trigger("falling")) j_k_ff_4 (
    .J(in_4), .clk(not_4_out), .K(in_4), .Q(out_8));  // open: Qn, preset, en, reset

  // Notes on the sheet:
  //   Row SET
  //   This is my set pin
  //   These are my outputs. In other words, the LEDS
  //   RESETS
endmodule

module CellSelector2 (
  input  in_1,
  input  in_2,
  input  in_3,
  input  in_4,
  output out_5,
  output out_6,
  output out_7,
  output out_8
);

  not not_1 (out_6, in_2);
  not not_2 (out_5, in_1);
  not not_3 (out_8, in_4);
  not not_4 (out_7, in_3);
endmodule

module _2x2 (
);

  wire and_1_out, and_2_out, and_3_out, and_4_out, button_1_out, button_2_out, button_3_out, button_4_out,
       j_k_ff_1_q, j_k_ff_2_q, j_k_ff_3_q, j_k_ff_4_q, not_1_out, not_2_out, not_3_out, not_4_out;

  not not_1 (not_1_out, button_1_out);
  Button button_1 (.out(button_1_out));
  J_K_Flip_Flop #(.trigger("falling")) j_k_ff_1 (
    .J(button_1_out), .clk(not_1_out), .K(not_1_out), .Q(j_k_ff_1_q));  // open: Qn, preset, en, reset
  not not_2 (not_2_out, button_2_out);
  Button button_2 (.out(button_2_out));
  J_K_Flip_Flop #(.trigger("falling")) j_k_ff_2 (
    .J(button_2_out), .clk(not_2_out), .K(not_2_out), .Q(j_k_ff_2_q));  // open: Qn, preset, en, reset
  not not_3 (not_3_out, button_3_out);
  Button button_3 (.out(button_3_out));
  J_K_Flip_Flop #(.trigger("falling")) j_k_ff_3 (
    .J(button_3_out), .clk(not_3_out), .K(not_3_out), .Q(j_k_ff_3_q));  // open: Qn, preset, en, reset
  LED led_1 (.in(and_1_out));
  and and_1 (and_1_out, j_k_ff_1_q, j_k_ff_3_q);
  and and_2 (and_2_out, j_k_ff_2_q, j_k_ff_3_q);
  LED led_2 (.in(and_2_out));
  not not_4 (not_4_out, button_4_out);
  Button button_4 (.out(button_4_out));
  J_K_Flip_Flop #(.trigger("falling")) j_k_ff_4 (
    .J(button_4_out), .clk(not_4_out), .K(not_4_out), .Q(j_k_ff_4_q));  // open: Qn, preset, en, reset
  and and_3 (and_3_out, j_k_ff_1_q, j_k_ff_4_q);
  LED led_3 (.in(and_3_out));
  and and_4 (and_4_out, j_k_ff_2_q, j_k_ff_4_q);
  LED led_4 (.in(and_4_out));
endmodule

module YO (
  input  [5:0] in_1,
  input  [5:0] in_2,
  output out_3,
  output out_4
);

  wire button_1_out, button_2_out;

  Button button_1 (.out(button_1_out));
  Button button_2 (.out(button_2_out));
  Half half_1 (.A(button_2_out), .B(button_1_out), .S(out_3), .C(out_4));
  DotMatrix #(.matrixcols(6), .matrixrows(6)) dotmatrix_1 (.col0(in_1), .col1(in_2));  // open: col2, col3, col4, col5
endmodule

module Half (
  input  A,
  input  B,
  output S,
  output C
);

  wire and_2_out, and_3_out, not_1_out, not_2_out;

  not not_1 (not_1_out, A);
  not not_2 (not_2_out, B);
  and and_1 (C, A, B);
  and and_2 (and_2_out, not_1_out, B);
  and and_3 (and_3_out, A, not_2_out);
  or or_1 (S, and_2_out, and_3_out);
endmodule
