// Logisim project SR.circ as structural Verilog: 3 circuits, main circuit main
module main (
  input  in_1,
  input  [1:0] in_2,
  input  in_3,
  input  in_4,
  input  in_5,
  input  in_6
);

  wire and_1_out, and_2_out, and_3_out, and_4_out, and_5_out, and_6_out, and_7_out, and_8_out, and_9_out,
       and_10_out, and_11_out, and_12_out, and_13_out, and_14_out, decoder_1_out0, decoder_1_out1,
       decoder_1_out2, decoder_1_out3, latch_1_out_3, latch_2_out_3, latch_3_out_3, latch_4_out_3,
       latch_5_out_3, latch_6_out_3, latch_7_out_3, latch_8_out_3, latch_9_out_3, latch_10_out_3,
       latch_11_out_3, latch_12_out_3, latch_13_out_3, latch_14_out_3, latch_15_out_3, latch_16_out_3,
       not_1_out, not_2_out, not_3_out, not_4_out;

  Decoder #(.select(2)) decoder_1 (
    .out0(decoder_1_out0), .out1(decoder_1_out1), .out2(decoder_1_out2), .out3(decoder_1_out3), .sel(in_2),
    .en(in_1));
  and and_1 (and_1_out, decoder_1_out0, not_1_out);
  Latch latch_1 (.R(and_1_out), .S(decoder_1_out0), .out_3(latch_1_out_3));
  and and_2 (and_2_out, decoder_1_out1, not_1_out);
  Latch latch_2 (.R(and_2_out), .S(decoder_1_out1), .out_3(latch_2_out_3));
  and and_3 (and_3_out, decoder_1_out2, not_1_out);
  Latch latch_3 (.R(and_3_out), .S(decoder_1_out2), .out_3(latch_3_out_3));
  Latch latch_4 (.S(decoder_1_out3), .out_3(latch_4_out_3));  // open: R
  not not_1 (not_1_out, in_3);
  and and_4 (and_4_out, decoder_1_out0, not_2_out);
  LED led_1 (.in(latch_1_out_3));
  and and_5 (and_5_out, decoder_1_out1, not_2_out);
  LED led_2 (.in(latch_2_out_3));
  and and_6 (and_6_out, decoder_1_out2, not_2_out);
  LED led_3 (.in(latch_3_out_3));
  LED led_4 (.in(latch_4_out_3));
  not not_2 (not_2_out, in_4);
  LED led_5 (.in(latch_5_out_3));
  Latch latch_5 (.R(and_4_out), .S(decoder_1_out0), .out_3(latch_5_out_3));
  Latch latch_6 (.R(and_5_out), .S(decoder_1_out1), .out_3(latch_6_out_3));
  LED led_6 (.in(latch_6_out_3));
  LED led_7 (.in(latch_7_out_3));
  Latch latch_7 (.R(and_6_out), .S(decoder_1_out2), .out_3(latch_7_out_3));
  LED led_8 (.in(latch_8_out_3));
  Latch latch_8 (.S(decoder_1_out3), .out_3(latch_8_out_3));  // open: R
  not not_3 (not_3_out, in_5);
  and and_7 (and_7_out, decoder_1_out0, not_3_out);
  Latch latch_9 (.R(and_7_out), .S(decoder_1_out0), .out_3(latch_9_out_3));
  LED led_9 (.in(latch_9_out_3));
  and and_8 (and_8_out, decoder_1_out1, not_3_out);
  LED led_10 (.in(latch_10_out_3));
  Latch latch_10 (.R(and_8_out), .S(decoder_1_out1), .out_3(latch_10_out_3));
  and and_9 (and_9_out, decoder_1_out2, not_3_out);
  Latch latch_11 (.R(and_9_out), .S(decoder_1_out2), .out_3(latch_11_out_3));
  LED led_11 (.in(latch_11_out_3));
  and and_10 (and_10_out, decoder_1_out3, not_3_out);
  LED led_12 (.in(latch_12_out_3));
  Latch latch_12 (.R(and_10_out), .S(decoder_1_out3), .out_3(latch_12_out_3));
  and and_11 (and_11_out, decoder_1_out0, not_4_out);
  Latch latch_13 (.R(and_11_out), .S(decoder_1_out0), .out_3(latch_13_out_3));
  and and_12 (and_12_out, decoder_1_out1, not_4_out);
  Latch latch_14 (.R(and_12_out), .S(decoder_1_out1), .out_3(latch_14_out_3));
  and and_13 (and_13_out, decoder_1_out2, not_4_out);
  Latch latch_15 (.R(and_13_out), .S(decoder_1_out2), .out_3(latch_15_out_3));
  and and_14 (and_14_out, decoder_1_out3, not_4_out);
  Latch latch_16 (.R(and_14_out), .S(decoder_1_out3), .out_3(latch_16_out_3));
  not not_4 (not_4_out, in_6);
  LED led_13 (.in(latch_13_out_3));
  LED led_14 (.in(latch_14_out_3));
  LED led_15 (.in(latch_15_out_3));
  LED led_16 (.in(latch_16_out_3));

  // Notes on the sheet:
  //   Turning of the Decoder is not a possibilty
endmodule

module Latch (
  input  R,
  input  S,
  output out_3
);

  wire nor_1_out, nor_2_out;

  nor nor_1 (nor_1_out, R, nor_2_out);
  nor nor_2 (nor_2_out, nor_1_out, S);
  xor xor_1 (out_3, nor_1_out, nor_2_out);
endmodule

module Main2 (
  input  in_1,
  input  [1:0] in_2,
  input  in_3,
  input  in_4,
  input  in_5,
  input  in_6
);

  wire decoder_1_out0, decoder_1_out1, decoder_1_out2, decoder_1_out3, latch_1_out_3, latch_2_out_3,
       latch_3_out_3, latch_4_out_3, latch_5_out_3, latch_6_out_3, latch_7_out_3, latch_8_out_3,
       latch_9_out_3, latch_10_out_3, latch_11_out_3, latch_12_out_3, latch_13_out_3, latch_14_out_3,
       latch_15_out_3, latch_16_out_3, not_1_out, not_2_out, not_3_out, not_4_out;

  Decoder #(.select(2)) decoder_1 (
    .out0(decoder_1_out0), .out1(decoder_1_out1), .out2(decoder_1_out2), .out3(decoder_1_out3), .sel(in_2),
    .en(in_1));
  Latch latch_1 (.R(not_1_out), .S(decoder_1_out0), .out_3(latch_1_out_3));
  Latch latch_2 (.R(not_1_out), .S(decoder_1_out1), .out_3(latch_2_out_3));
  Latch latch_3 (.R(not_1_out), .S(decoder_1_out2), .out_3(latch_3_out_3));
  Latch latch_4 (.R(not_1_out), .S(decoder_1_out3), .out_3(latch_4_out_3));
  not not_1 (not_1_out, in_3);
  LED led_1 (.in(latch_1_out_3));
  LED led_2 (.in(latch_2_out_3));
  LED led_3 (.in(latch_3_out_3));
  LED led_4 (.in(latch_4_out_3));
  not not_2 (not_2_out, in_4);
  LED led_5 (.in(latch_5_out_3));
  Latch latch_5 (.R(not_2_out), .S(decoder_1_out0), .out_3(latch_5_out_3));
  LED led_6 (.in(latch_6_out_3));
  Latch latch_6 (.R(not_2_out), .S(decoder_1_out1), .out_3(latch_6_out_3));
  LED led_7 (.in(latch_7_out_3));
  Latch latch_7 (.R(not_2_out), .S(decoder_1_out2), .out_3(latch_7_out_3));
  LED led_8 (.in(latch_8_out_3));
  Latch latch_8 (.R(not_2_out), .S(decoder_1_out3), .out_3(latch_8_out_3));
  not not_3 (not_3_out, in_5);
  Latch latch_9 (.R(not_3_out), .S(decoder_1_out0), .out_3(latch_9_out_3));
  LED led_9 (.in(latch_9_out_3));
  Latch latch_10 (.R(not_3_out), .S(decoder_1_out1), .out_3(latch_10_out_3));
  LED led_10 (.in(latch_10_out_3));
  LED led_11 (.in(latch_11_out_3));
  Latch latch_11 (.R(not_3_out), .S(decoder_1_out2), .out_3(latch_11_out_3));
  Latch latch_12 (.R(not_3_out), .S(decoder_1_out3), .out_3(latch_12_out_3));
  LED led_12 (.in(latch_12_out_3));
  Latch latch_13 (.R(not_4_out), .S(decoder_1_out0), .out_3(latch_13_out_3));
  Latch latch_14 (.R(not_4_out), .S(decoder_1_out1), .out_3(latch_14_out_3));
  Latch latch_15 (.R(not_4_out), .S(decoder_1_out2), .out_3(latch_15_out_3));
  Latch latch_16 (.R(not_4_out), .S(decoder_1_out3), .out_3(latch_16_out_3));
  not not_4 (not_4_out, in_6);
  LED led_13 (.in(latch_13_out_3));
  LED led_14 (.in(latch_14_out_3));
  LED led_15 (.in(latch_15_out_3));
  LED led_16 (.in(latch_16_out_3));

  // Notes on the sheet:
  //   Turning of the Decoder is not a possibilty
endmodule
