// Logisim project test.circ as structural Verilog: 2 circuits, main circuit main
module main (
  input  in_1,
  input  in_2,
  output out_3,
  output out_4
);

  wire button_1_out;

  Button button_1 (.out(button_1_out));
  J_K_Flip_Flop j_k_ff_1 (.J(in_1), .clk(button_1_out), .K(in_2), .Q(out_3), .Qn(out_4));  // open: preset, en, reset
endmodule

module rows (
  input  in_1,
  input  in_2,
  input  in_3,
  input  in_4,
  input  in_5,
  input  in_6,
  input  in_7,
  input  in_8,
  input  in_9,
  input  in_10,
  input  in_11,
  input  in_12,
  input  in_13,
  input  in_14,
  input  in_15,
  input  in_16,
  input  in_17,
  input  in_18,
  input  in_19,
  input  in_20,
  input  in_21,
  input  in_22,
  input  in_23,
  input  in_24,
  input  in_25,
  input  in_26,
  input  in_27,
  input  in_28,
  input  in_29,
  input  in_30,
  input  in_31,
  input  in_32,
  input  in_33,
  input  in_34,
  input  in_35,
  input  in_36,
  output out_37,
  output [2:0] out_38,
  output out_39
);

  wire or_1_out, or_2_out, or_3_out, priority_encoder_1_p4, priority_encoder_1_p6, priority_encoder_1_p7;

  or or_1 (or_1_out, in_1, in_2, in_3, in_4, in_5, in_6);
  or or_2 (or_2_out, in_7, in_8, in_9, in_10, in_11, in_12);
  or or_3 (or_3_out, in_13, in_14, in_15, in_16, in_17, in_18);
  // Priority_Encoder priority_encoder_1: pin names not known; wires that end beside it: or_1_out, or_2_out, or_3_out, priority_encoder_1_p4, out_38, priority_encoder_1_p6, priority_encoder_1_p7
  or or_4 (priority_encoder_1_p4, in_19, in_20, in_21, in_22, in_23, in_24);
  or or_5 (priority_encoder_1_p6, in_25, in_26, in_27, in_28, in_29, in_30);
  LED led_1 (.in(in_1));
  or or_6 (priority_encoder_1_p7, in_31, in_32, in_33, in_34, in_35, in_36);
  LED led_2 (.in(in_2));
  LED led_3 (.in(in_7));
  LED led_4 (.in(in_13));
  LED led_5 (.in(in_3));
  LED led_6 (.in(in_8));
  LED led_7 (.in(in_9));
  LED led_8 (.in(in_14));
  LED led_9 (.in(in_19));
  LED led_10 (.in(in_25));
  Multiplexer #(.select(3), .enable("false")) multiplexer_1 (
    .in0(in_1), .in1(in_7), .in2(in_13), .in3(in_19), .in4(in_25), .in5(in_31), .out(out_37), .sel(out_38));  // open: in6, in7
  LED led_11 (.in(in_4));
  LED led_12 (.in(in_10));
  LED led_13 (.in(in_15));
  LED led_14 (.in(in_20));
  LED led_15 (.in(in_21));
  LED led_16 (.in(in_26));
  LED led_17 (.in(in_31));
  LED led_18 (.in(in_5));
  LED led_19 (.in(in_11));
  LED led_20 (.in(in_16));
  LED led_21 (.in(in_22));
  LED led_22 (.in(in_27));
  LED led_23 (.in(in_33));
  LED led_24 (.in(in_32));
  Multiplexer #(.select(3), .enable("false")) multiplexer_2 (
    .in0(in_2), .in1(in_8), .in2(in_14), .in3(in_20), .in4(in_26), .in5(in_32), .out(out_39), .sel(out_38));  // open: in6, in7
  LED led_25 (.in(in_6));
  LED led_26 (.in(in_12));
  LED led_27 (.in(in_17));
  LED led_28 (.in(in_23));
  LED led_29 (.in(in_28));
  LED led_30 (.in(in_34));
  LED led_31 (.in(in_18));
  LED led_32 (.in(in_24));
  LED led_33 (.in(in_29));
  LED led_34 (.in(in_35));
  LED led_35 (.in(in_30));
  LED led_36 (.in(in_36));
endmodule
