// Logisim project test1.circ as structural Verilog: 3 circuits, main circuit main
module main (
  input  in_1,
  input  in_2,
  input  [2:0] in_3,
  input  [2:0] in_4,
  input  in_5,
  output out_6,
  output out_7,
  output out_8,
  output out_9,
  output out_10,
  output out_11,
  output out_12,
  output out_13,
  output out_14,
  output out_15,
  output out_16,
  output out_17,
  output out_18,
  output out_19,
  output out_20,
  output out_21
);

  wire decoder_1_out0, decoder_1_out1, decoder_1_out2, decoder_1_out3, decoder_2_out0, decoder_2_out1,
       decoder_2_out2, decoder_2_out3;

  Decoder #(.select(3)) decoder_1 (
    .out0(decoder_1_out0), .out1(decoder_1_out1), .out2(decoder_1_out2), .out3(decoder_1_out3), .sel(in_3),
    .en(in_2));  // open: out4, out5, out6, out7
  LED led_1 (.in_2(decoder_2_out0), .out_4(out_6), .in_3(decoder_1_out0), .in_1(in_1));
  LED led_2 (.in_2(decoder_2_out0), .out_4(out_10), .in_3(decoder_1_out1), .in_1(in_1));
  LED led_3 (.in_2(decoder_2_out0), .out_4(out_14), .in_3(decoder_1_out2), .in_1(in_1));
  LED led_4 (.in_2(decoder_2_out0), .out_4(out_18), .in_3(decoder_1_out3), .in_1(in_1));
  LED led_5 (.in_2(decoder_2_out1), .out_4(out_7), .in_3(decoder_1_out0), .in_1(in_1));
  LED led_6 (.in_2(decoder_2_out1), .out_4(out_11), .in_3(decoder_1_out1), .in_1(in_1));
  LED led_7 (.in_2(decoder_2_out1), .out_4(out_15), .in_3(decoder_1_out2), .in_1(in_1));
  LED led_8 (.in_2(decoder_2_out1), .out_4(out_19), .in_3(decoder_1_out3), .in_1(in_1));
  Decoder #(.select(3)) decoder_2 (
    .out0(decoder_2_out0), .out1(decoder_2_out1), .out2(decoder_2_out2), .out3(decoder_2_out3), .sel(in_4),
    .en(in_5));  // open: out4, out5, out6, out7
  LED led_9 (.in_2(decoder_2_out2), .out_4(out_8), .in_3(decoder_1_out0), .in_1(in_1));
  LED led_10 (.in_2(decoder_2_out2), .out_4(out_12), .in_3(decoder_1_out1), .in_1(in_1));
  LED led_11 (.in_2(decoder_2_out2), .out_4(out_16), .in_3(decoder_1_out2), .in_1(in_1));
  LED led_12 (.in_2(decoder_2_out2), .out_4(out_20), .in_3(decoder_1_out3), .in_1(in_1));
  LED led_13 (.in_2(decoder_2_out3), .out_4(out_9), .in_3(decoder_1_out0), .in_1(in_1));
  LED led_14 (.in_2(decoder_2_out3), .out_4(out_13), .in_3(decoder_1_out1), .in_1(in_1));
  LED led_15 (.in_2(decoder_2_out3), .out_4(out_17), .in_3(decoder_1_out2), .in_1(in_1));
  LED led_16 (.in_2(decoder_2_out3), .out_4(out_21), .in_3(decoder_1_out3), .in_1(in_1));
endmodule

module LED (
  input  in_1,
  input  in_2,
  input  in_3,
  output out_4
);

  wire j_k_ff_1_q, j_k_ff_2_q, not_1_out, not_2_out;

  not not_1 (not_1_out, in_2);
  not not_2 (not_2_out, in_3);
  J_K_Flip_Flop #(.trigger("falling")) j_k_ff_1 (
    .J(in_1), .clk(not_1_out), .K(in_1), .Q(j_k_ff_1_q));  // open: Qn, preset, en, reset
  J_K_Flip_Flop #(.trigger("falling")) j_k_ff_2 (
    .J(in_1), .clk(not_2_out), .K(in_1), .Q(j_k_ff_2_q));  // open: Qn, preset, en, reset
  and and_1 (out_4, j_k_ff_1_q, j_k_ff_2_q);
endmodule

module Decoder_test (
  input  [1:0] in_1,
  input  in_2
);

  wire decoder_1_out0, decoder_1_out1, decoder_1_out2, decoder_1_out3;

  Decoder #(.select(2)) decoder_1 (
    .out0(decoder_1_out0), .out1(decoder_1_out1), .out2(decoder_1_out2), .out3(decoder_1_out3), .sel(in_1),
    .en(in_2));
  LED_part led_1 (.in(decoder_1_out0));
  LED_part led_2 (.in(decoder_1_out1));
  LED_part led_3 (.in(decoder_1_out2));
  LED_part led_4 (.in(decoder_1_out3));
endmodule
